# Fritzing sketch Chessboard (saved by Fritzing 0.9.3b)
circuit board: 8.46667cm x 5.64444cm
breadboards: 1

parts:
  LED1 = LED - 5mm [color="Red (633nm)" package="5 mm [THT]"]
  LED2 = LED - 5mm [color="Red (633nm)" package="5 mm [THT]"]
  LED3 = LED - 5mm [color="Red (633nm)" package="5 mm [THT]"]
  LED4 = LED - 5mm [color="Red (633nm)" package="5 mm [THT]"]
  LED5 = LED - 5mm [color="Red (633nm)" package="5 mm [THT]"]
  LED6 = LED - 5mm [color="Red (633nm)" package="5 mm [THT]"]
  LED7 = LED - 5mm [color="Red (633nm)" package="5 mm [THT]"]
  LED8 = LED - 5mm [color="Red (633nm)" package="5 mm [THT]"]
  LED9 = LED - 5mm [color="Red (633nm)" package="5 mm [THT]"]
  LED10 = LED - 5mm [color="Red (633nm)" package="5 mm [THT]"]
  LED11 = LED - 5mm [color="Red (633nm)" package="5 mm [THT]"]
  LED12 = LED - 5mm [color="Red (633nm)" package="5 mm [THT]"]
  LED13 = LED - 5mm [color="Red (633nm)" package="5 mm [THT]"]
  LED14 = LED - 5mm [color="Red (633nm)" package="5 mm [THT]"]
  LED15 = LED - 5mm [color="Red (633nm)" package="5 mm [THT]"]
  LED16 = LED - 5mm [color="Red (633nm)" package="5 mm [THT]"]
  LED17 = LED - 5mm [color="Red (633nm)" package="5 mm [THT]"]
  LED18 = LED - 5mm [color="Red (633nm)" package="5 mm [THT]"]
  Part1 = HT16K33 Breakout 16x8 LED Matrix Driver [part_number=1427]
  LED82 = LED - 5mm [color="Red (633nm)" package="5 mm [THT]"]
  LED83 = LED - 5mm [color="Red (633nm)" package="5 mm [THT]"]
  LED84 = LED - 5mm [color="Red (633nm)" package="5 mm [THT]"]
  LED85 = LED - 5mm [color="Red (633nm)" package="5 mm [THT]"]
  LED86 = LED - 5mm [color="Red (633nm)" package="5 mm [THT]"]
  LED87 = LED - 5mm [color="Red (633nm)" package="5 mm [THT]"]
  LED88 = LED - 5mm [color="Red (633nm)" package="5 mm [THT]"]
  LED89 = LED - 5mm [color="Red (633nm)" package="5 mm [THT]"]
  LED90 = LED - 5mm [color="Red (633nm)" package="5 mm [THT]"]
  LED91 = LED - 5mm [color="Red (633nm)" package="5 mm [THT]"]
  LED92 = LED - 5mm [color="Red (633nm)" package="5 mm [THT]"]
  LED93 = LED - 5mm [color="Red (633nm)" package="5 mm [THT]"]
  LED94 = LED - 5mm [color="Red (633nm)" package="5 mm [THT]"]
  LED95 = LED - 5mm [color="Red (633nm)" package="5 mm [THT]"]
  LED96 = LED - 5mm [color="Red (633nm)" package="5 mm [THT]"]
  LED97 = LED - 5mm [color="Red (633nm)" package="5 mm [THT]"]
  LED99 = LED - 5mm [color="Red (633nm)" package="5 mm [THT]"]
  LED100 = LED - 5mm [color="Red (633nm)" package="5 mm [THT]"]
  LED101 = LED - 5mm [color="Red (633nm)" package="5 mm [THT]"]
  LED102 = LED - 5mm [color="Red (633nm)" package="5 mm [THT]"]
  LED103 = LED - 5mm [color="Red (633nm)" package="5 mm [THT]"]
  LED104 = LED - 5mm [color="Red (633nm)" package="5 mm [THT]"]
  LED105 = LED - 5mm [color="Red (633nm)" package="5 mm [THT]"]
  LED106 = LED - 5mm [color="Red (633nm)" package="5 mm [THT]"]
  LED107 = LED - 5mm [color="Red (633nm)" package="5 mm [THT]"]
  LED108 = LED - 5mm [color="Red (633nm)" package="5 mm [THT]"]
  LED109 = LED - 5mm [color="Red (633nm)" package="5 mm [THT]"]
  LED110 = LED - 5mm [color="Red (633nm)" package="5 mm [THT]"]
  LED111 = LED - 5mm [color="Red (633nm)" package="5 mm [THT]"]
  LED112 = LED - 5mm [color="Red (633nm)" package="5 mm [THT]"]
  LED113 = LED - 5mm [color="Red (633nm)" package="5 mm [THT]"]
  LED114 = LED - 5mm [color="Red (633nm)" package="5 mm [THT]"]
  LED115 = LED - 5mm [color="Red (633nm)" package="5 mm [THT]"]
  LED116 = LED - 5mm [color="Red (633nm)" package="5 mm [THT]"]
  LED117 = LED - 5mm [color="Red (633nm)" package="5 mm [THT]"]
  LED118 = LED - 5mm [color="Red (633nm)" package="5 mm [THT]"]
  LED119 = LED - 5mm [color="Red (633nm)" package="5 mm [THT]"]
  LED120 = LED - 5mm [color="Red (633nm)" package="5 mm [THT]"]
  LED121 = LED - 5mm [color="Red (633nm)" package="5 mm [THT]"]
  LED122 = LED - 5mm [color="Red (633nm)" package="5 mm [THT]"]
  LED123 = LED - 5mm [color="Red (633nm)" package="5 mm [THT]"]
  LED124 = LED - 5mm [color="Red (633nm)" package="5 mm [THT]"]
  LED125 = LED - 5mm [color="Red (633nm)" package="5 mm [THT]"]
  LED126 = LED - 5mm [color="Red (633nm)" package="5 mm [THT]"]
  LED127 = LED - 5mm [color="Red (633nm)" package="5 mm [THT]"]
  LED128 = LED - 5mm [color="Red (633nm)" package="5 mm [THT]"]
  LED129 = LED - 5mm [color="Red (633nm)" package="5 mm [THT]"]
  LED131 = LED - 5mm [color="Red (633nm)" package="5 mm [THT]"]
  LED133 = LED - 5mm [color="Red (633nm)" package="5 mm [THT]"]
  LED136 = LED - 5mm [color="Red (633nm)" package="5 mm [THT]"]
  LED137 = LED - 5mm [color="Red (633nm)" package="5 mm [THT]"]
  LED139 = LED - 5mm [color="Red (633nm)" package="5 mm [THT]"]
  LED141 = LED - 5mm [color="Red (633nm)" package="5 mm [THT]"]
  LED144 = LED - 5mm [color="Red (633nm)" package="5 mm [THT]"]
  LED98 = LED - 5mm [color="Red (633nm)" package="5 mm [THT]"]
  IC2 = IC, DIP package, 16 pins [chip_label=4017]
  S63 = Reed switch [package=THT]
  D8 = Rectifier Diode [part_number=1N4001 package="300 mil [THT]"]
  S71 = Reed switch [package=THT]
  D13 = Rectifier Diode [part_number=1N4001 package="300 mil [THT]"]
  S79 = Reed switch [package=THT]
  D21 = Rectifier Diode [part_number=1N4001 package="300 mil [THT]"]
  S87 = Reed switch [package=THT]
  D29 = Rectifier Diode [part_number=1N4001 package="300 mil [THT]"]
  S114 = Reed switch [package=THT]
  S115 = Reed switch [package=THT]
  S116 = Reed switch [package=THT]
  S119 = Reed switch [package=THT]
  D38 = Rectifier Diode [part_number=1N4001 package="300 mil [THT]"]
  D42 = Rectifier Diode [part_number=1N4001 package="300 mil [THT]"]
  D43 = Rectifier Diode [part_number=1N4001 package="300 mil [THT]"]
  D46 = Rectifier Diode [part_number=1N4001 package="300 mil [THT]"]
  IC3 = IC, DIP package, 16 pins [chip_label=4021]
  S120 = Reed switch [package=THT]
  S121 = Reed switch [package=THT]
  S122 = Reed switch [package=THT]
  S123 = Reed switch [package=THT]
  S124 = Reed switch [package=THT]
  S125 = Reed switch [package=THT]
  S126 = Reed switch [package=THT]
  S127 = Reed switch [package=THT]
  D47 = Rectifier Diode [part_number=1N4001 package="300 mil [THT]"]
  D48 = Rectifier Diode [part_number=1N4001 package="300 mil [THT]"]
  D49 = Rectifier Diode [part_number=1N4001 package="300 mil [THT]"]
  D50 = Rectifier Diode [part_number=1N4001 package="300 mil [THT]"]
  D51 = Rectifier Diode [part_number=1N4001 package="300 mil [THT]"]
  D52 = Rectifier Diode [part_number=1N4001 package="300 mil [THT]"]
  D53 = Rectifier Diode [part_number=1N4001 package="300 mil [THT]"]
  D54 = Rectifier Diode [part_number=1N4001 package="300 mil [THT]"]
  S128 = Reed switch [package=THT]
  S129 = Reed switch [package=THT]
  S130 = Reed switch [package=THT]
  S131 = Reed switch [package=THT]
  S132 = Reed switch [package=THT]
  S133 = Reed switch [package=THT]
  S134 = Reed switch [package=THT]
  S135 = Reed switch [package=THT]
  S136 = Reed switch [package=THT]
  S137 = Reed switch [package=THT]
  S138 = Reed switch [package=THT]
  S139 = Reed switch [package=THT]
  S140 = Reed switch [package=THT]
  S141 = Reed switch [package=THT]
  S142 = Reed switch [package=THT]
  S143 = Reed switch [package=THT]
  D55 = Rectifier Diode [part_number=1N4001 package="300 mil [THT]"]
  D56 = Rectifier Diode [part_number=1N4001 package="300 mil [THT]"]
  D57 = Rectifier Diode [part_number=1N4001 package="300 mil [THT]"]
  D58 = Rectifier Diode [part_number=1N4001 package="300 mil [THT]"]
  D59 = Rectifier Diode [part_number=1N4001 package="300 mil [THT]"]
  D60 = Rectifier Diode [part_number=1N4001 package="300 mil [THT]"]
  D61 = Rectifier Diode [part_number=1N4001 package="300 mil [THT]"]
  D62 = Rectifier Diode [part_number=1N4001 package="300 mil [THT]"]
  D63 = Rectifier Diode [part_number=1N4001 package="300 mil [THT]"]
  D64 = Rectifier Diode [part_number=1N4001 package="300 mil [THT]"]
  D65 = Rectifier Diode [part_number=1N4001 package="300 mil [THT]"]
  D66 = Rectifier Diode [part_number=1N4001 package="300 mil [THT]"]
  D67 = Rectifier Diode [part_number=1N4001 package="300 mil [THT]"]
  D68 = Rectifier Diode [part_number=1N4001 package="300 mil [THT]"]
  D69 = Rectifier Diode [part_number=1N4001 package="300 mil [THT]"]
  D70 = Rectifier Diode [part_number=1N4001 package="300 mil [THT]"]
  S144 = Reed switch [package=THT]
  S145 = Reed switch [package=THT]
  S146 = Reed switch [package=THT]
  S147 = Reed switch [package=THT]
  S148 = Reed switch [package=THT]
  S149 = Reed switch [package=THT]
  S150 = Reed switch [package=THT]
  S151 = Reed switch [package=THT]
  S152 = Reed switch [package=THT]
  S153 = Reed switch [package=THT]
  S154 = Reed switch [package=THT]
  S155 = Reed switch [package=THT]
  S156 = Reed switch [package=THT]
  S157 = Reed switch [package=THT]
  S158 = Reed switch [package=THT]
  S159 = Reed switch [package=THT]
  S160 = Reed switch [package=THT]
  S161 = Reed switch [package=THT]
  S162 = Reed switch [package=THT]
  S163 = Reed switch [package=THT]
  S164 = Reed switch [package=THT]
  S165 = Reed switch [package=THT]
  S166 = Reed switch [package=THT]
  S167 = Reed switch [package=THT]
  S168 = Reed switch [package=THT]
  S169 = Reed switch [package=THT]
  S170 = Reed switch [package=THT]
  S171 = Reed switch [package=THT]
  S172 = Reed switch [package=THT]
  S173 = Reed switch [package=THT]
  S174 = Reed switch [package=THT]
  S175 = Reed switch [package=THT]
  D71 = Rectifier Diode [part_number=1N4001 package="300 mil [THT]"]
  D72 = Rectifier Diode [part_number=1N4001 package="300 mil [THT]"]
  D73 = Rectifier Diode [part_number=1N4001 package="300 mil [THT]"]
  D74 = Rectifier Diode [part_number=1N4001 package="300 mil [THT]"]
  D75 = Rectifier Diode [part_number=1N4001 package="300 mil [THT]"]
  D76 = Rectifier Diode [part_number=1N4001 package="300 mil [THT]"]
  D77 = Rectifier Diode [part_number=1N4001 package="300 mil [THT]"]
  D78 = Rectifier Diode [part_number=1N4001 package="300 mil [THT]"]
  D79 = Rectifier Diode [part_number=1N4001 package="300 mil [THT]"]
  D80 = Rectifier Diode [part_number=1N4001 package="300 mil [THT]"]
  D81 = Rectifier Diode [part_number=1N4001 package="300 mil [THT]"]
  D82 = Rectifier Diode [part_number=1N4001 package="300 mil [THT]"]
  D83 = Rectifier Diode [part_number=1N4001 package="300 mil [THT]"]
  D84 = Rectifier Diode [part_number=1N4001 package="300 mil [THT]"]
  D85 = Rectifier Diode [part_number=1N4001 package="300 mil [THT]"]
  D86 = Rectifier Diode [part_number=1N4001 package="300 mil [THT]"]
  D87 = Rectifier Diode [part_number=1N4001 package="300 mil [THT]"]
  D88 = Rectifier Diode [part_number=1N4001 package="300 mil [THT]"]
  D89 = Rectifier Diode [part_number=1N4001 package="300 mil [THT]"]
  D90 = Rectifier Diode [part_number=1N4001 package="300 mil [THT]"]
  D91 = Rectifier Diode [part_number=1N4001 package="300 mil [THT]"]
  D92 = Rectifier Diode [part_number=1N4001 package="300 mil [THT]"]
  D93 = Rectifier Diode [part_number=1N4001 package="300 mil [THT]"]
  D94 = Rectifier Diode [part_number=1N4001 package="300 mil [THT]"]
  D95 = Rectifier Diode [part_number=1N4001 package="300 mil [THT]"]
  D96 = Rectifier Diode [part_number=1N4001 package="300 mil [THT]"]
  D97 = Rectifier Diode [part_number=1N4001 package="300 mil [THT]"]
  D98 = Rectifier Diode [part_number=1N4001 package="300 mil [THT]"]
  D99 = Rectifier Diode [part_number=1N4001 package="300 mil [THT]"]
  D100 = Rectifier Diode [part_number=1N4001 package="300 mil [THT]"]
  D101 = Rectifier Diode [part_number=1N4001 package="300 mil [THT]"]
  D102 = Rectifier Diode [part_number=1N4001 package="300 mil [THT]"]
  R1 = Resistor [tolerance=±5% resistance=220 package=THT]
  R2 = Resistor [tolerance=±5% resistance=220 package=THT]
  R3 = Resistor [tolerance=±5% resistance=220 package=THT]
  R4 = Resistor [tolerance=±5% resistance=220 package=THT]
  R5 = Resistor [tolerance=±5% resistance=220 package=THT]
  R6 = Resistor [tolerance=±5% resistance=220 package=THT]
  R7 = Resistor [tolerance=±5% resistance=220 package=THT]
  R8 = Resistor [tolerance=±5% resistance=220 package=THT]
  Part2 = Arduino Uno (Rev3)
  S184 = Pushbutton [package="[THT]"]
  D103 = Rectifier Diode [part_number=1N4001 package="300 mil [THT]"]
  D104 = Rectifier Diode [part_number=1N4001 package="300 mil [THT]"]
  S185 = Pushbutton [package="[THT]"]
  D105 = Rectifier Diode [part_number=1N4001 package="300 mil [THT]"]
  D106 = Rectifier Diode [part_number=1N4001 package="300 mil [THT]"]
  S186 = Pushbutton [package="[THT]"]
  S187 = Pushbutton [package="[THT]"]
  D107 = Rectifier Diode [part_number=1N4001 package="300 mil [THT]"]
  S188 = Pushbutton [package="[THT]"]
  D108 = Rectifier Diode [part_number=1N4001 package="300 mil [THT]"]
  D109 = Rectifier Diode [part_number=1N4001 package="300 mil [THT]"]
  D110 = Rectifier Diode [part_number=1N4001 package="300 mil [THT]"]
  S189 = Pushbutton [package="[THT]"]
  S190 = Pushbutton [package="[THT]"]
  S191 = Pushbutton [package="[THT]"]
  LED145 = LED - 5mm [color="Red (633nm)" package="5 mm [THT]"]
  LED146 = LED - 5mm [color="Red (633nm)" package="5 mm [THT]"]
  LED147 = LED - 5mm [color="Red (633nm)" package="5 mm [THT]"]
  LED148 = LED - 5mm [color="Red (633nm)" package="5 mm [THT]"]
  LED149 = LED - 5mm [color="Red (633nm)" package="5 mm [THT]"]
  LED150 = LED - 5mm [color="Red (633nm)" package="5 mm [THT]"]
  LED151 = LED - 5mm [color="Red (633nm)" package="5 mm [THT]"]
  LED152 = LED - 5mm [color="Red (633nm)" package="5 mm [THT]"]
  LCD1 = LCD screen  # not connected

nets:
  N1: LED1.cathode, LED2.cathode, LED3.cathode, LED4.cathode, LED5.cathode, LED6.cathode, LED7.cathode, LED8.cathode, LED9.cathode, Part1.C0, LED136.cathode, LED152.cathode
  N2: LED1.anode, LED17.anode, Part1.A2, LED84.anode, LED93.anode, LED107.anode, LED111.anode, LED125.anode, LED129.anode
  N3: LED2.anode, LED13.anode, Part1.A1, LED82.anode, LED102.anode, LED103.anode, LED120.anode, LED121.anode, LED139.anode
  N4: LED3.anode, LED16.anode, Part1.A3, LED89.anode, LED91.anode, LED109.anode, LED116.anode, LED127.anode, LED98.anode
  N5: LED4.anode, LED10.anode, Part1.A0, LED88.anode, LED99.anode, LED101.anode, LED117.anode, LED119.anode, LED137.anode
  N6: LED5.anode, LED14.anode, Part1.A4, LED83.anode, LED96.anode, LED97.anode, LED114.anode, LED115.anode, LED133.anode
  N7: LED6.anode, LED11.anode, Part1.A5, LED90.anode, LED94.anode, LED95.anode, LED112.anode, LED113.anode, LED131.anode
  N8: LED7.anode, LED18.anode, Part1.A6, LED87.anode, LED92.anode, LED104.anode, LED110.anode, LED122.anode, LED128.anode
  N9: LED8.anode, LED15.anode, Part1.A7, LED85.anode, LED100.anode, LED105.anode, LED118.anode, LED123.anode, LED141.anode
  N10: LED9.anode, LED12.anode, Part1.A8, LED86.anode, LED106.anode, LED108.anode, LED124.anode, LED126.anode, LED144.anode
  N11: LED10.cathode, LED11.cathode, LED12.cathode, LED13.cathode, LED14.cathode, LED15.cathode, LED16.cathode, LED17.cathode, LED18.cathode, Part1.C1, LED151.cathode
  N12: Part1.A10, LED136.anode
  N13: Part1.A9, LED146.anode, LED147.anode, LED148.anode, LED149.anode, LED150.anode, LED151.anode, LED152.anode
  N14: Part1.C2, LED82.cathode, LED83.cathode, LED84.cathode, LED85.cathode, LED86.cathode, LED87.cathode, LED88.cathode, LED89.cathode, LED90.cathode, LED150.cathode
  N15: Part1.C3, LED91.cathode, LED92.cathode, LED93.cathode, LED95.cathode, LED97.cathode, LED101.cathode, LED103.cathode, LED105.cathode, LED108.cathode, LED148.cathode
  N16: Part1.C4, LED94.cathode, LED96.cathode, LED99.cathode, LED100.cathode, LED102.cathode, LED104.cathode, LED106.cathode, LED107.cathode, LED98.cathode, LED149.cathode
  N17: Part1.C5, LED109.cathode, LED110.cathode, LED111.cathode, LED113.cathode, LED115.cathode, LED119.cathode, LED121.cathode, LED123.cathode, LED126.cathode, LED146.cathode
  N18: Part1.C6, LED112.cathode, LED114.cathode, LED116.cathode, LED117.cathode, LED118.cathode, LED120.cathode, LED122.cathode, LED124.cathode, LED125.cathode, LED147.cathode
  N19: Part1.C7, LED127.cathode, LED128.cathode, LED129.cathode, LED131.cathode, LED133.cathode, LED137.cathode, LED139.cathode, LED141.cathode, LED144.cathode, LED145.cathode
  N20: IC2.pin1, D29.anode, D54.anode, D58.anode, D62.anode, D75.anode, D85.anode, D97.anode, D102.anode
  N21: IC2.pin2, D42.anode, D51.anode, D55.anode, D67.anode, D73.anode, D82.anode, D98.anode, D101.anode
  N22: IC2.pin4, D46.anode, D53.anode, D68.anode, D69.anode, D76.anode, D80.anode, D81.anode, D90.anode
  N23: IC2.pin5, D21.anode, D49.anode, D56.anode, D59.anode, D79.anode, D83.anode, D84.anode, D99.anode
  N24: IC2.pin6, D13.anode, D52.anode, D64.anode, D66.anode, D71.anode, D89.anode, D92.anode, D96.anode
  N25: IC2.pin7, D38.anode, D48.anode, D61.anode, D65.anode, D72.anode, D74.anode, D78.anode, D94.anode
  N26: IC2.pin9, D8.anode, D50.anode, D57.anode, D60.anode, D77.anode, D86.anode, D88.anode, D95.anode
  N27: IC2.pin10, D43.anode, D47.anode, D63.anode, D70.anode, D87.anode, D91.anode, D93.anode, D100.anode
  N28: IC2.pin11, D103.anode, D104.anode, D105.anode, D106.anode, D107.anode, D108.anode, D109.anode, D110.anode
  N29: IC2.pin14, Part2.D5_PWM
  N30: IC2.pin15, Part2.D6_PWM
  N31: S63.pin_1, D8.cathode
  N32: S63.pin_2, S71.pin_2, S79.pin_2, S87.pin_2, S114.pin_2, S115.pin_2, S116.pin_2, S119.pin_2, IC3.pin7, R4.Pin_0, S190.Pin_3, S190.Pin_4
  N33: S71.pin_1, D13.cathode
  N34: S79.pin_1, D21.cathode
  N35: S87.pin_1, D29.cathode
  N36: S114.pin_1, D38.cathode
  N37: S115.pin_1, D46.cathode
  N38: S116.pin_1, D42.cathode
  N39: S119.pin_1, D43.cathode
  N40: IC3.pin1, S146.pin_2, S148.pin_2, S150.pin_2, S152.pin_2, S161.pin_2, S164.pin_2, S169.pin_2, S175.pin_2, R5.Pin_0, S184.Pin_3, S184.Pin_4
  N41: IC3.pin3, Part2.D2
  N42: IC3.pin4, S128.pin_2, S131.pin_2, S134.pin_2, S135.pin_2, S136.pin_2, S138.pin_2, S139.pin_2, S143.pin_2, R7.Pin_0, S188.Pin_3, S188.Pin_4
  N43: IC3.pin5, S129.pin_2, S130.pin_2, S132.pin_2, S133.pin_2, S137.pin_2, S140.pin_2, S141.pin_2, S142.pin_2, R6.Pin_0, S189.Pin_3, S189.Pin_4
  N44: IC3.pin6, S120.pin_2, S121.pin_2, S122.pin_2, S123.pin_2, S124.pin_2, S125.pin_2, S126.pin_2, S127.pin_2, R8.Pin_0, S191.Pin_3, S191.Pin_4
  N45: IC3.pin9, Part2.D3_PWM
  N46: IC3.pin10, Part2.D4
  N47: IC3.pin13, S147.pin_2, S151.pin_2, S154.pin_2, S159.pin_2, S168.pin_2, S170.pin_2, S172.pin_2, S174.pin_2, R3.Pin_0, S186.Pin_3, S186.Pin_4
  N48: IC3.pin14, S145.pin_2, S156.pin_2, S157.pin_2, S158.pin_2, S160.pin_2, S162.pin_2, S163.pin_2, S171.pin_2, R2.Pin_0, S187.Pin_3, S187.Pin_4
  N49: IC3.pin15, S144.pin_2, S149.pin_2, S153.pin_2, S155.pin_2, S165.pin_2, S166.pin_2, S167.pin_2, S173.pin_2, R1.Pin_0, S185.Pin_3, S185.Pin_4
  N50: S120.pin_1, D49.cathode
  N51: S121.pin_1, D54.cathode
  N52: S122.pin_1, D52.cathode
  N53: S123.pin_1, D53.cathode
  N54: S124.pin_1, D48.cathode
  N55: S125.pin_1, D47.cathode
  N56: S126.pin_1, D51.cathode
  N57: S127.pin_1, D50.cathode
  N58: S128.pin_1, D62.cathode
  N59: S129.pin_1, D58.cathode
  N60: S130.pin_1, D66.cathode
  N61: S131.pin_1, D69.cathode
  N62: S132.pin_1, D55.cathode
  N63: S133.pin_1, D68.cathode
  N64: S134.pin_1, D57.cathode
  N65: S135.pin_1, D59.cathode
  N66: S136.pin_1, D64.cathode
  N67: S137.pin_1, D60.cathode
  N68: S138.pin_1, D67.cathode
  N69: S139.pin_1, D65.cathode
  N70: S140.pin_1, D56.cathode
  N71: S141.pin_1, D70.cathode
  N72: S142.pin_1, D61.cathode
  N73: S143.pin_1, D63.cathode
  N74: S144.pin_1, D98.cathode
  N75: S145.pin_1, D82.cathode
  N76: S146.pin_1, D91.cathode
  N77: S147.pin_1, D73.cathode
  N78: S148.pin_1, D72.cathode
  N79: S149.pin_1, D85.cathode
  N80: S150.pin_1, D76.cathode
  N81: S151.pin_1, D93.cathode
  N82: S152.pin_1, D77.cathode
  N83: S153.pin_1, D87.cathode
  N84: S154.pin_1, D86.cathode
  N85: S155.pin_1, D99.cathode
  N86: S156.pin_1, D94.cathode
  N87: S157.pin_1, D97.cathode
  N88: S158.pin_1, D80.cathode
  N89: S159.pin_1, D84.cathode
  N90: S160.pin_1, D92.cathode
  N91: S161.pin_1, D83.cathode
  N92: S162.pin_1, D95.cathode
  N93: S163.pin_1, D79.cathode
  N94: S164.pin_1, D101.cathode
  N95: S165.pin_1, D96.cathode
  N96: S166.pin_1, D81.cathode
  N97: S167.pin_1, D78.cathode
  N98: S168.pin_1, D75.cathode
  N99: S169.pin_1, D102.cathode
  N100: S170.pin_1, D89.cathode
  N101: S171.pin_1, D100.cathode
  N102: S172.pin_1, D74.cathode
  N103: S173.pin_1, D88.cathode
  N104: S174.pin_1, D90.cathode
  N105: S175.pin_1, D71.cathode
  GND: R1.Pin_1, R2.Pin_1, R3.Pin_1, R4.Pin_1, R5.Pin_1, R6.Pin_1, R7.Pin_1, R8.Pin_1
  N106: S184.Pin_1, S184.Pin_2, D103.cathode
  N107: D104.cathode, S185.Pin_1, S185.Pin_2
  N108: D105.cathode, S186.Pin_1, S186.Pin_2
  N109: D106.cathode, S187.Pin_1, S187.Pin_2
  N110: D107.cathode, S188.Pin_1, S188.Pin_2
  N111: D108.cathode, S191.Pin_1, S191.Pin_2
  N112: D109.cathode, S189.Pin_1, S189.Pin_2
  N113: D110.cathode, S190.Pin_1, S190.Pin_2

notes:
  A1
  B1
  A2
  H1
  Buttons for menu
  A9
  C1
  D1
  E1
  F1
  G1
  H9
  PullDown resiistors 20k
  I1
  I9
  I2
  I8
  A3
  A4
  A6
  A7
  A5
  A8
  B2
  B3
  B7
  B6
  B5
  B4
  B9
  I7
  I5
  I6
  I3
  I4
  Chessboard LED's 9*9

custom parts:
  HT16K33 Breakout 16x8 LED Matrix Driver: This is the magic sauce in our 7-segment and matrix backpacks, now available in breadboard-friendly breakout board format. The HT16K33 is a neat little chip that has the ability to drive a multiplexed 16x8 matrix (that's 128 individual LEDs). The communication protocol is I2C so it uses only 2 pins, and you can have up to 8 selectable I2C addresses so thats a total of 8 matrices, each one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
